# Fritzing sketch mfrc_reader (saved by Fritzing 0.9.2b)
circuit board: 9.2035cm x 6.67186cm
breadboards: 1

parts:
  Součástka1 = Arduino Nano (Rev3.0)
  R1 = Resistor [tolerance=±5% resistance=10k part_number=R1 package=THT]
  R2 = Resistor [tolerance=±5% resistance=10k part_number=R2 package=THT]
  JP1 = Header 4 [part_number=P1 package=screwterminal-3.5mm-4_lock]
  Součástka2 = RFID-RC522-v2

nets:
  GND: Součástka1.GND, JP1.4, Součástka2.GND
  N1: Součástka1.D9, Součástka2.RST
  N2: Součástka1.D10, Součástka2.SDA
  N3: Součástka1.D11/MOSI, Součástka2.MOSI
  N4: Součástka1.D12/MISO, Součástka2.MISO
  5V: Součástka1.5V, R1.Pin_1, R2.Pin_1, JP1.1
  N5: Součástka1.A5, R1.Pin_0, JP1.3
  N6: Součástka1.A4, R2.Pin_0, JP1.2
  3V3: Součástka1.3V3, Součástka2.3.3V
  N7: Součástka1.D13/SCK, Součástka2.SCK

custom parts:
  RFID-RC522-v2: A simple China made RFID-RC522 Reader; do check the pin labels, as this is a MFRC522 based clone.
